# Fritzing sketch pumpkin_ultrasonic (saved by Fritzing 0.8.3b)
circuit board: 16.9333cm x 5.64444cm

parts:
  LED1 = LED - 5mm [color="Yellow (595nm)" package="5 mm [THT]"]
  R1 = Resistor [tolerance=±5% resistance=220 package=THT]
  Bauteil1 = Arduino Board Ethernet
  LED2 = LED - 5mm [color="Red (635nm)" package="5 mm [THT]"]
  R2 = Resistor [tolerance=±5% resistance=220 package=THT]
  LED4 = LED - 5mm [color="Red (633nm)" package="5 mm [THT]"]
  LED5 = LED - 5mm [color="Red (633nm)" package="5 mm [THT]"]
  LED6 = LED - 5mm [color="Red (633nm)" package="5 mm [THT]"]
  R3 = Resistor [tolerance=±5% resistance=15 package=THT]
  BC547 = NPN-Transistor [package="TO92 [THT]"]
  SPKR1 = Loudspeaker
  Bauteil2 = SRF05 Ultrasonic Rangefinder

nets:
  GND: LED1.cathode, Bauteil1.GND, LED2.cathode, LED4.cathode, LED5.cathode, LED6.cathode, SPKR1.pin1, Bauteil2.GND
  N1: LED1.anode, R1.Pin_0
  N2: R1.Pin_1, Bauteil1.D5_PWM
  N3: Bauteil1.D8, Bauteil2.Echo
  N4: Bauteil1.D11/MOSI, SPKR1.pin2
  N5: Bauteil1.D4, BC547.B
  N6: Bauteil1.D6_PWM, R2.Pin_1
  N7: Bauteil1.D7, Bauteil2.Trig
  5V: Bauteil1.5V, BC547.C, Bauteil2.VCC
  N8: LED2.anode, R2.Pin_0
  N9: LED4.anode, LED5.anode, LED6.anode, R3.Pin_0
  N10: R3.Pin_1, BC547.E

notes:
  RED_LEDS
  YELLOW_CANDLE_LED
  RED_CANDLE_LED
